# Fritzing sketch DHT11 with LCD I2C (saved by Fritzing 0.9.3b)
breadboards: 1

parts:
  Componente1 = Arduino Uno (Rev3)
  Part1 = LCD1602-I2C
  R1 = Resistor [tolerance=±5% resistance=68 package="0402 [SMD]"]

nets:
  N1: Componente1.A4/SDA, Part1.SDA
  N2: Componente1.A5/SCL, Part1.SCL
  N3: Componente1.5V, R1.Pin_1
  GND: Componente1.GND, Part1.GND
  N4: Part1.VCC, R1.Pin_0

custom parts:
  LCD1602-I2C: A standard character display, usually with 2x16 characters. Comes in many colors with LCM1602 IIC attached.
