# Fritzing sketch Light_Sensor_with_LED (saved by Fritzing 0.9.3b)
breadboards: 1

parts:
  Part1 = Arduino Uno (Rev3) - ICSP
  LED1 = LEDs [package=led10mm]
  R1 = Resistor [tolerance=±5% resistance=220 package="0402 [SMD]"]
  R2 = PHOTOCELL [package=photocell-kit]
  R3 = Resistor [tolerance=±5% resistance=220 package="0402 [SMD]"]

nets:
  N1: Part1.A0, R2.P$2, R3.Pin_0
  N2: Part1.D9_PWM, R1.Pin_1
  N3: Part1.5V, R2.P$1
  N4: Part1.GND, LED1.C, R3.Pin_1
