# Fritzing sketch Sound_sensor_with_LED (saved by Fritzing 0.9.3b)
breadboards: 1

parts:
  Part1 = Arduino Uno (Rev3) - ICSP
  R1 = Resistor [tolerance=±5% resistance=68 package="1206 [SMD]"]
  LED1 = LEDs [package=led10mm]
  Part2 = Breakout Board for Electret Microphone

nets:
  N1: Part1.D13/SCK, R1.Pin_1
  GND: Part1.GND, LED1.C, Part2.GND
  N2: Part1.D2, Part2.VCC
  N3: Part1.5V, Part2.AUD
  N4: R1.Pin_0, LED1.A
